# Fritzing sketch schematic (saved by Fritzing 0.9.3b)

parts:
  Arduino_Nano = Arduino Nano (Rev3.0)
  HC-06 = Bluetooth HC-06
  HX711 = HX711 Weighing Sensor Module
  R1 = Resistor [tolerance=±5% resistance=1k package=THT]
  R2 = Resistor [tolerance=±5% resistance=2.2k package=THT]
  J1 = LOAD_CELL [package=1x03]
  J2 = LOAD_CELL [package=1x03]
  J3 = LOAD_CELL [package=1x03]
  J4 = LOAD_CELL [package=1x03]
  R3 = Resistor [tolerance=±5% resistance=800k package=THT]
  R4 = Resistor [tolerance=±5% resistance=800k package=THT]

nets:
  GND: Arduino_Nano.GND, HC-06.GND, HX711.GND, R2.Pin_0
  N1: Arduino_Nano.D2, HC-06.TXD
  N2: Arduino_Nano.D3, R1.Pin_1
  N3: Arduino_Nano.D4, R3.Pin_1
  N4: Arduino_Nano.D5, R4.Pin_1
  5V: Arduino_Nano.5V, HX711.VCC
  N5: Arduino_Nano.A5, R4.Pin_0
  N6: Arduino_Nano.A4, R3.Pin_0
  N7: Arduino_Nano.A1, HX711.DO/RX
  N8: Arduino_Nano.A0, HX711.CK/TX
  3V3: Arduino_Nano.3V3, HC-06.VCC
  N9: HC-06.RXD, R1.Pin_0, R2.Pin_1
  N10: HX711.E+, J1.W
  N11: HX711.E-, J3.W
  N12: HX711.A+, J2.W
  N13: HX711.A-, J4.W
  N14: J1.B, J4.B
  N15: J1.R, J2.R
  N16: J2.B, J3.B
  N17: J3.R, J4.R

notes:
  B W R
  R W B
  Tare Capacitive Button
  Mode Capacitive Button
